# Fritzing sketch ESP32 PCB (saved by Fritzing 1.0.5)
circuit board: 2.75264cm x 2.61693cm

parts:
  U1 = ESP32S-HiLetgo [part_number=ESP32S]
  J1 = AVR ISP 6 Pin [package=2x3]

nets:
  N1: U1.3.3, J1.5
  N2: U1.GPIO21, J1.2
  N3: U1.GPIO22, J1.1
  N4: U1.GND, J1.6

notes:
  Ignore labels for I2C connector

custom parts:
  ESP32S-HiLetgo: HiLetgo ESP-WROOM-32 ESP32 ESP-32S Development Board 2.4GHz Dual-Mode WiFi + Bluetooth Dual Cores Microcontroller The ESP32 integrated with Antenna switches, RF Balun, power amplifiers, low-noise amplifiers, filters, and management modules, and the entire solution occupies the least area of PCB. 2.4 GHz Wi-Fi plus Bluetooth dual-mode chip, with TSMC Ultra-low power consumption 40nm technology,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
