# Fritzing sketch ESP32 breadboard (saved by Fritzing 1.0.5)
breadboards: 1

parts:
  U1 = ESP32S-HiLetgo [part_number=ESP32S]
  J1 = female pin header, 6 pins [form="♀ (female)" part_number="Ribbon cable"]

nets:
  N1: U1.3.3, J1.pin1
  N2: U1.GND, J1.pin2
  N3: U1.GPIO21, J1.pin6
  N4: U1.GPIO22, J1.pin5

custom parts:
  ESP32S-HiLetgo: HiLetgo ESP-WROOM-32 ESP32 ESP-32S Development Board 2.4GHz Dual-Mode WiFi + Bluetooth Dual Cores Microcontroller The ESP32 integrated with Antenna switches, RF Balun, power amplifiers, low-noise amplifiers, filters, and management modules, and the entire solution occupies the least area of PCB. 2.4 GHz Wi-Fi plus Bluetooth dual-mode chip, with TSMC Ultra-low power consumption 40nm technology,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
